// Logisim project CPU_logisim_V1.0_提交封存版.circ as structural Verilog: 11 circuits, main circuit main
module main (
  input  reset,
  output [31:0] out_2,
  output out_3,
  output [4:0] out_4,
  output [31:0] out_5,
  output MemWrite,
  output [4:0] out_7,
  output [31:0] out_8
);

  wire clk, zero;
  wire [1:0] EXTOp, MemtoReg, NPCOp, RegDst, SrcB;
  wire [2:0] ALUOp;
  wire [4:0] _10_6, _15_11, _20_16, _25_21;
  wire [5:0] funct, opcode;
  wire [15:0] IMM16;
  wire [25:0] IMM26;
  wire [31:0] A, ALUResult, B, DMRD, extedIMM, npc_1_npc, pc_1_pc;

  Clock clock_1 (.out(clk));
  PC pc_1 (.PC_prime(npc_1_npc), .clr(reset), .PC(pc_1_pc), .clk(clk));
  NPC npc_1 (.PC(pc_1_pc), .imm26(IMM26), .zero(zero), .NPCOp(NPCOp), .NPC(npc_1_npc), .imm16(IMM16));  // open: RA, PC4
  IM im_1 (.PC(pc_1_pc), .instr(out_2));  // open: reset
  // Probe on ALUOp
  controller controller_1 (
    .instr(out_2), .ALUOp(ALUOp), .EXTOp(EXTOp), .DMWr(MemWrite), .RFWr(out_3), .zero(zero),
    .MemtoReg(MemtoReg), .regdst(RegDst), .SrcB(SrcB), .NPCOp(NPCOp));
  general_splitter general_splitter_1 (
    ._32_bit_input(out_2), .opcode(opcode), ._25_21(_25_21), ._20_16(_20_16), ._15_11(_15_11), ._10_6(_10_6),
    .funct(funct), .IMM16(IMM16), .out_9(IMM26));
  Multiplexer #(.select(2), .width(5)) multiplexer_1 (
    .in0(_15_11), .in1(_20_16), .out(out_4), .sel(RegDst));  // open: in2, in3, en
  EXT ext_1 (.imm(IMM16), .EXTOp(EXTOp), .exted_imm(extedIMM));
  GRF grf_1 (
    .clk(clk), .WE(out_3), .A1(_25_21), .reset(reset), .A2(_20_16), .WD(out_5), .A3(out_4), .RD1(A),
    .RD2(out_8));
  Multiplexer #(.select(2), .width(32)) multiplexer_2 (
    .in0(out_8), .in1(extedIMM), .out(B), .sel(SrcB));  // open: in2, in3, en
  ALU alu_1 (.A(A), .B(B), .ALUOp(ALUOp), .\output ({ALUResult[31:7], out_7, ALUResult[1:0]}), .zero(zero));
  DM dm_1 (
    .A({ALUResult[31:7], out_7, ALUResult[1:0]}), .WD(out_8), .clk(clk), .clr(reset), .DMWr(MemWrite),
    .RD(DMRD));
  Multiplexer #(.select(2), .width(32)) multiplexer_3 (
    .in0({ALUResult[31:7], out_7, ALUResult[1:0]}), .in1(DMRD), .out(out_5), .sel(MemtoReg));  // open: in2, in3, en
  // Probe on MemtoReg

  // Other names for the same wires on the sheet: A1[4:0] = _25_21; A2[4:0] = _20_16; ALUResult[6:2] = out_7;
  //   MemAddr[4:0] = out_7; DMWr = MemWrite; Instr[31:0] = out_2; RD1[31:0] = A; MemData[31:0] = out_8;
  //   RD2[31:0] = out_8; A3[4:0] = out_4; RegAddr[4:0] = out_4; RegWrite = out_3; RFWr = out_3; rst = reset;
  //   RegData[31:0] = out_5; WD[31:0] = out_5

  // Notes on the sheet:
  //   io tunnel
  //   PC
  //   General Splitter
  //   NPC
  //   choose A1
  //   choose A2
  //   choose A3
  //   GRF
  //   choose ALU B
  //   need a mux
  //   ALU
  //   DM
  //   choose mem to store in RGF
  //   choose WD
endmodule

module PC (
  input  [31:0] PC_prime,
  input  clr,
  input  clk,
  output [31:0] PC
);

  Register #(.width(32)) register_1 (.D(PC_prime), .Q(PC), .clk(clk), .clr(clr));  // open: en

  // Other names for the same wires on the sheet: reset = clr

  // Notes on the sheet:
  //   io tunnel
  //   function area
endmodule

module NPC (
  input  [31:0] PC,
  input  [25:0] imm26,
  input  [15:0] imm16,
  input  zero,
  input  [1:0] NPCOp,
  input  [31:0] RA,
  output [31:0] PC4,
  output [31:0] NPC
);

  wire [15:0] shifter_1_out;
  wire [31:0] adder_2_out, bit_extender_1_out, multiplexer_1_out, PCBranch;

  Adder #(.width(32)) adder_1 (.a(PC), .b(32'h4), .out(PC4));  // open: cin, cout
  Adder #(.width(32)) adder_2 (.a(PC), .b(32'h4), .out(adder_2_out));  // open: cin, cout
  Shifter #(.width(16)) shifter_1 (.in(imm16), .\dist (4'b0010), .out(shifter_1_out));
  // Probe on shifter_1_out
  assign bit_extender_1_out = {{16{shifter_1_out[15]}}, shifter_1_out};  // Bit_Extender bit_extender_1
  // Probe on bit_extender_1_out
  // Probe on PCBranch
  Adder #(.width(32)) adder_3 (.a(adder_2_out), .b(bit_extender_1_out), .out(PCBranch));  // open: cin, cout
  Multiplexer #(.width(32)) multiplexer_1 (.in0(PC4), .in1(PCBranch), .out(multiplexer_1_out), .sel(zero));  // open: en
  Multiplexer #(.select(2), .width(32)) multiplexer_2 (
    .in0(PC4), .in1(multiplexer_1_out), .out(NPC), .sel(NPCOp));  // open: in2, in3, en

  // Notes on the sheet:
  //   io tunnel
  //   Process  area
  //   calc PC+4
  //   calc PCbranch
endmodule

module general_splitter (
  input  [31:0] _32_bit_input,
  output [5:0] opcode,
  output [4:0] _25_21,
  output [4:0] _20_16,
  output [4:0] _15_11,
  output [4:0] _10_6,
  output [5:0] funct,
  output [15:0] IMM16,
  output [25:0] out_9
);


  assign _10_6 = _32_bit_input[10:6];
  assign _15_11 = _32_bit_input[15:11];
  assign _20_16 = _32_bit_input[20:16];
  assign _25_21 = _32_bit_input[25:21];
  assign funct = _32_bit_input[5:0];
  assign IMM16 = _32_bit_input[15:0];
  assign opcode = _32_bit_input[31:26];
  assign out_9 = _32_bit_input[25:0];

  // Other names for the same wires on the sheet: IMM26[25:0] = _32_bit_input[25:0]; input[31:0] = _32_bit_input

  // Notes on the sheet:
  //   io tunnel
  //   process
endmodule

module IM (
  input  [31:0] PC,
  input  reset,
  output [31:0] instr
);

  ROM #(.addrWidth(5), .dataWidth(32)) rom_1 (.addr(PC[6:2]), .data(instr));  // open: sel

  // Other names for the same wires on the sheet: clr = reset; addr[4:0] = PC[6:2]

  // Notes on the sheet:
  //   io tunnel
  //   process
  //   contents of rom_1 (hex, n*v repeats v):
  //   35080064 ac080000
endmodule

module GRF (
  input  clk,
  input  WE,
  input  [4:0] A1,
  input  reset,
  input  [4:0] A2,
  input  [31:0] WD,
  input  [4:0] A3,
  output [31:0] RD1,
  output [31:0] RD2
);

  wire [31:0] reg0, reg0out, reg1, reg1out, reg2, reg2out, reg3, reg3out, reg4, reg4out, reg5, reg5out, reg6,
       reg6out, reg7, reg7out, reg8, reg8out, reg9, reg9out, reg10, reg10out, reg11, reg11out, reg12,
       reg12out, reg13, reg13out, reg14, reg14out, reg15, reg15out, reg16, reg16out, reg17, reg17out, reg18,
       reg18out, reg19, reg19out, reg20, reg20out, reg21, reg21out, reg22, reg22out, reg23, reg23out, reg24,
       reg24out, reg25, reg25out, reg26, reg26out, reg27, reg27out, reg28, reg28out, reg29, reg29out, reg30,
       reg30out, reg31, reg31out;

  Register #(.width(32)) register_1 (.D(reg0), .Q(reg0out), .clk(clk), .clr(reset));  // open: en
  Register #(.width(32)) register_2 (.D(reg4), .Q(reg4out), .clk(clk), .clr(reset));  // open: en
  Register #(.width(32)) register_3 (.D(reg8), .Q(reg8out), .clk(clk), .clr(reset));  // open: en
  Register #(.width(32)) register_4 (.D(reg12), .Q(reg12out), .clk(clk), .clr(reset));  // open: en
  Register #(.width(32)) register_5 (.D(reg16), .Q(reg16out), .clk(clk), .clr(reset));  // open: en
  Register #(.width(32)) register_6 (.D(reg20), .Q(reg20out), .clk(clk), .clr(reset));  // open: en
  Register #(.width(32)) register_7 (.D(reg24), .Q(reg24out), .clk(clk), .clr(reset));  // open: en
  Register #(.width(32)) register_8 (.D(reg28), .Q(reg28out), .clk(clk), .clr(reset));  // open: en
  Demultiplexer #(.select(5), .width(32), .tristate("true")) demultiplexer_1 (
    .out0(reg0), .out1(reg1), .out2(reg2), .out3(reg3), .out4(reg4), .out5(reg5), .out6(reg6), .out7(reg7),
    .out8(reg8), .out9(reg9), .out10(reg10), .out11(reg11), .out12(reg12), .out13(reg13), .out14(reg14),
    .out15(reg15), .out16(reg16), .out17(reg17), .out18(reg18), .out19(reg19), .out20(reg20), .out21(reg21),
    .out22(reg22), .out23(reg23), .out24(reg24), .out25(reg25), .out26(reg26), .out27(reg27), .out28(reg28),
    .out29(reg29), .out30(reg30), .out31(reg31), .in(WD), .sel(A3), .en(WE));
  Register #(.width(32)) register_9 (.D(reg1), .Q(reg1out), .clk(clk), .clr(reset));  // open: en
  Register #(.width(32)) register_10 (.D(reg5), .Q(reg5out), .clk(clk), .clr(reset));  // open: en
  Register #(.width(32)) register_11 (.D(reg9), .Q(reg9out), .clk(clk), .clr(reset));  // open: en
  Register #(.width(32)) register_12 (.D(reg13), .Q(reg13out), .clk(clk), .clr(reset));  // open: en
  Register #(.width(32)) register_13 (.D(reg17), .Q(reg17out), .clk(clk), .clr(reset));  // open: en
  Register #(.width(32)) register_14 (.D(reg21), .Q(reg21out), .clk(clk), .clr(reset));  // open: en
  Register #(.width(32)) register_15 (.D(reg25), .Q(reg25out), .clk(clk), .clr(reset));  // open: en
  Register #(.width(32)) register_16 (.D(reg29), .Q(reg29out), .clk(clk), .clr(reset));  // open: en
  Register #(.width(32)) register_17 (.D(reg2), .Q(reg2out), .clk(clk), .clr(reset));  // open: en
  Register #(.width(32)) register_18 (.D(reg6), .Q(reg6out), .clk(clk), .clr(reset));  // open: en
  Register #(.width(32)) register_19 (.D(reg10), .Q(reg10out), .clk(clk), .clr(reset));  // open: en
  Register #(.width(32)) register_20 (.D(reg14), .Q(reg14out), .clk(clk), .clr(reset));  // open: en
  Register #(.width(32)) register_21 (.D(reg18), .Q(reg18out), .clk(clk), .clr(reset));  // open: en
  Register #(.width(32)) register_22 (.D(reg22), .Q(reg22out), .clk(clk), .clr(reset));  // open: en
  Register #(.width(32)) register_23 (.D(reg26), .Q(reg26out), .clk(clk), .clr(reset));  // open: en
  Register #(.width(32)) register_24 (.D(reg30), .Q(reg30out), .clk(clk), .clr(reset));  // open: en
  Multiplexer #(.select(5), .width(32)) multiplexer_1 (
    .in0({32{1'b0}}), .in1(reg1out), .in2(reg2out), .in3(reg3out), .in4(reg4out), .in5(reg5out),
    .in6(reg6out), .in7(reg7out), .in8(reg8out), .in9(reg9out), .in10(reg10out), .in11(reg11out),
    .in12(reg12out), .in13(reg13out), .in14(reg14out), .in15(reg15out), .in16(reg16out), .in17(reg17out),
    .in18(reg18out), .in19(reg19out), .in20(reg20out), .in21(reg21out), .in22(reg22out), .in23(reg23out),
    .in24(reg24out), .in25(reg25out), .in26(reg26out), .in27(reg27out), .in28(reg28out), .in29(reg29out),
    .in30(reg30out), .in31(reg31out), .out(RD1), .sel(A1));  // open: en
  Register #(.width(32)) register_25 (.D(reg3), .Q(reg3out), .clk(clk), .clr(reset));  // open: en
  Register #(.width(32)) register_26 (.D(reg7), .Q(reg7out), .clk(clk), .clr(reset));  // open: en
  Register #(.width(32)) register_27 (.D(reg11), .Q(reg11out), .clk(clk), .clr(reset));  // open: en
  Register #(.width(32)) register_28 (.D(reg15), .Q(reg15out), .clk(clk), .clr(reset));  // open: en
  Register #(.width(32)) register_29 (.D(reg19), .Q(reg19out), .clk(clk), .clr(reset));  // open: en
  Register #(.width(32)) register_30 (.D(reg23), .Q(reg23out), .clk(clk), .clr(reset));  // open: en
  Register #(.width(32)) register_31 (.D(reg27), .Q(reg27out), .clk(clk), .clr(reset));  // open: en
  Register #(.width(32)) register_32 (.D(reg31), .Q(reg31out), .clk(clk), .clr(reset));  // open: en
  Multiplexer #(.select(5), .width(32)) multiplexer_2 (
    .in0({32{1'b0}}), .in1(reg1out), .in2(reg2out), .in3(reg3out), .in4(reg4out), .in5(reg5out),
    .in6(reg6out), .in7(reg7out), .in8(reg8out), .in9(reg9out), .in10(reg10out), .in11(reg11out),
    .in12(reg12out), .in13(reg13out), .in14(reg14out), .in15(reg15out), .in16(reg16out), .in17(reg17out),
    .in18(reg18out), .in19(reg19out), .in20(reg20out), .in21(reg21out), .in22(reg22out), .in23(reg23out),
    .in24(reg24out), .in25(reg25out), .in26(reg26out), .in27(reg27out), .in28(reg28out), .in29(reg29out),
    .in30(reg30out), .in31(reg31out), .out(RD2), .sel(A2));  // open: en

  // Other names for the same wires on the sheet: rst = reset

  // Notes on the sheet:
  //   signial
  //   Write
  //   Read
endmodule

module EXT (
  input  [15:0] imm,
  input  [1:0] EXTOp,
  output [31:0] exted_imm
);

  wire [31:0] sExt, usExt;

  assign usExt = {{16{1'b0}}, imm};  // Bit_Extender bit_extender_1
  assign sExt = {{16{imm[15]}}, imm};  // Bit_Extender bit_extender_2
  Multiplexer #(.select(2), .width(32)) multiplexer_1 (
    .in0(usExt), .in1(sExt), .in2({imm, {16{1'b0}}}), .out(exted_imm), .sel(EXTOp));  // open: in3, en
  // Probe on exted_imm

  // Other names for the same wires on the sheet: extended_output[31:0] = exted_imm; ll16Ext[31:16] = imm

  // Notes on the sheet:
  //   io tunnel
  //   unsigned extend
  //   signed extend
  //   logicial left 16 bits
endmodule

module ALU (
  input  [31:0] A,
  input  [31:0] B,
  input  [2:0] ALUOp,
  output [31:0] \output ,
  output zero
);

  wire [31:0] A_B, A_B_t, AorB, BorIMM;

  // Probe on \output 
  Adder #(.width(32)) adder_1 (.a(A), .b(B), .out(A_B));  // open: cin, cout
  Subtractor #(.width(32)) subtractor_1 (.a(A), .b(B), .out(A_B_t));  // open: bin, bout
  assign AorB = A | B;  // OR_Gate or_1, 32 bits wide
  Shifter #(.width(32)) shifter_1 (.in(B), .\dist (5'b10000), .out(BorIMM));
  // Probe on B
  // Probe on AorB
  Comparator #(.width(32), .mode("unsigned")) comparator_1 (.a(\output ), .b({32{1'b0}}), .eq(zero));  // open: gt, lt
  Multiplexer #(.select(3), .width(32)) multiplexer_1 (
    .in0(A_B), .in1(A_B_t), .in2(AorB), .in3(BorIMM), .out(\output ), .sel(ALUOp));  // open: in4, in5, in6, in7, en
  // Probe on \output 

  // Notes on the sheet:
  //   io tunnel
  //   process
  //   A+B
  //   A-B
  //   AorB
  //   B or IMM
endmodule

module DM (
  input  [31:0] A,
  input  [31:0] WD,
  input  clk,
  input  clr,
  input  DMWr,
  output [31:0] RD
);

  RAM #(.addrWidth(5), .dataWidth(32), .bus("separate")) ram_1 (
    .addr(A[6:2]), .din(WD), .data(RD), .str(DMWr), .clk(clk), .clr(clr));  // open: sel, ld

  // Other names for the same wires on the sheet: A2_6[4:0] = A[6:2]

  // Notes on the sheet:
  //   io tunnel
  //   process
  //   calc A2-6
endmodule

// DMWr
module controller (
  input  [31:0] instr,
  input  zero,
  output [2:0] ALUOp,
  output [1:0] EXTOp,
  output DMWr,
  output RFWr,
  output [1:0] MemtoReg,
  output [1:0] regdst,
  output [1:0] SrcB,
  output [1:0] NPCOp
);

  wire addu, beq, comparator_1_eq, comparator_2_eq, comparator_3_eq, comparator_4_eq, lui, lw, nop, or_1_out,
       or_2_out, or_3_out, or_4_out, or_5_out, or_7_out, or_9_out, or_10_out, ori, priority_encoder_1_gs,
       priority_encoder_2_gs, priority_encoder_3_gs, priority_encoder_5_gs, priority_encoder_6_gs, subu, sw;
  wire [1:0] priority_encoder_2_out, priority_encoder_3_out, priority_encoder_5_out, priority_encoder_6_out;
  wire [2:0] priority_encoder_1_out;
  wire [4:0] _10_6, _15_11, _20_16, _25_21;
  wire [5:0] funct, opcode;

  Comparator #(.width(6), .mode("unsigned")) comparator_1 (
    .a(opcode), .b({6{1'b0}}), .eq(comparator_1_eq));  // open: gt, lt
  Comparator #(.width(6), .mode("unsigned")) comparator_2 (
    .a(funct), .b(6'b100001), .eq(comparator_2_eq));  // open: gt, lt
  // Probe on 6'b100001
  Comparator #(.width(6), .mode("unsigned")) comparator_3 (
    .a(opcode), .b({6{1'b0}}), .eq(comparator_3_eq));  // open: gt, lt
  Comparator #(.width(6), .mode("unsigned")) comparator_4 (
    .a(funct), .b(6'b100011), .eq(comparator_4_eq));  // open: gt, lt
  // Probe on 6'b100011
  Comparator #(.width(6), .mode("unsigned")) comparator_5 (.a(opcode), .b(6'b001101), .eq(ori));  // open: gt, lt
  // Probe on 6'b001101
  Comparator #(.width(6), .mode("unsigned")) comparator_6 (.a(opcode), .b(6'b100011), .eq(lw));  // open: gt, lt
  // Probe on 6'b100011
  and and_1 (addu, comparator_1_eq, comparator_2_eq);
  and and_2 (subu, comparator_3_eq, comparator_4_eq);
  general_splitter general_splitter_1 (
    ._32_bit_input(instr), .opcode(opcode), ._25_21(_25_21), ._20_16(_20_16), ._15_11(_15_11), ._10_6(_10_6),
    .funct(funct));  // open: IMM16, out_9
  // Probe on funct
  // Probe on 6'b000100
  // Probe on 6'b101011
  Comparator #(.width(6), .mode("unsigned")) comparator_7 (.a(opcode), .b(6'b101011), .eq(sw));  // open: gt, lt
  Comparator #(.width(6), .mode("unsigned")) comparator_8 (.a(opcode), .b(6'b000100), .eq(beq));  // open: gt, lt
  Comparator #(.width(6), .mode("unsigned")) comparator_9 (.a(opcode), .b(6'b001111), .eq(lui));  // open: gt, lt
  Comparator #(.width(32), .mode("unsigned")) comparator_10 (.a(instr), .b({32{1'b0}}), .eq(nop));  // open: gt, lt
  or or_1 (or_1_out, subu, beq);
  or or_2 (or_2_out, addu, lw, sw);
  or or_3 (or_3_out, addu, subu, lui);
  or or_4 (or_4_out, addu, subu, beq);
  or or_5 (or_5_out, ori, lw, sw, lui);
  Priority_Encoder priority_encoder_1 (
    .in0(or_2_out), .in1(or_1_out), .in2(ori), .in3(lui), .out(priority_encoder_1_out),
    .gs(priority_encoder_1_gs));  // open: in4, in5, in6, in7, en_in, en_out
  // Probe on priority_encoder_2_out
  Priority_Encoder #(.select(2)) priority_encoder_2 (
    .in0(or_3_out), .in1(lw), .out(priority_encoder_2_out), .gs(priority_encoder_2_gs));  // open: in2, in3, en_out, en_in
  buf or_6 (DMWr, sw);  // OR_Gate
  // Probe on priority_encoder_3_out
  Priority_Encoder #(.select(2)) priority_encoder_3 (
    .in0(or_4_out), .in1(or_5_out), .out(priority_encoder_3_out), .gs(priority_encoder_3_gs));  // open: in2, in3, en_out, en_in
  Multiplexer #(.width(3)) multiplexer_1 (
    .in0(3'b000), .in1(priority_encoder_1_out), .out(ALUOp), .sel(priority_encoder_1_gs));  // open: en
  // Probe on ALUOp
  // Probe on MemtoReg
  Multiplexer #(.width(2)) multiplexer_2 (
    .in0(2'b00), .in1(priority_encoder_2_out), .out(MemtoReg), .sel(priority_encoder_2_gs));  // open: en
  // Probe on SrcB
  Multiplexer #(.width(2)) multiplexer_3 (
    .in0(2'b00), .in1(priority_encoder_3_out), .out(SrcB), .sel(priority_encoder_3_gs));  // open: en
  or or_7 (or_7_out, lw, sw, lui);
  Priority_Encoder #(.select(2)) priority_encoder_4 (
    .in0(ori), .in1(or_7_out), .out(EXTOp));  // open: in2, in3, gs, en_out, en_in
  or or_8 (RFWr, lw, addu, subu, ori, lui);
  or or_9 (or_9_out, addu, subu);
  or or_10 (or_10_out, ori, lw, lui);
  Priority_Encoder #(.select(2)) priority_encoder_5 (
    .in1(beq), .out(priority_encoder_5_out), .gs(priority_encoder_5_gs));  // open: in0, in2, in3, en_out, en_in
  Multiplexer #(.width(2)) multiplexer_4 (
    .in0(2'b00), .in1(priority_encoder_5_out), .out(NPCOp), .sel(priority_encoder_5_gs));  // open: en
  Priority_Encoder #(.select(2)) priority_encoder_6 (
    .in0(or_9_out), .in1(or_10_out), .out(priority_encoder_6_out), .gs(priority_encoder_6_gs));  // open: in2, in3, en_out, en_in
  // Probe on regdst
  Multiplexer #(.width(2)) multiplexer_5 (
    .in0(2'b00), .in1(priority_encoder_6_out), .out(regdst), .sel(priority_encoder_6_gs));  // open: en

  // Notes on the sheet:
  //   io tunnel
  //   judge addu
  //   judge subu
  //   judge ori
  //   judge lw
  //   split
  //   judge beq
  //   judge lui
  //   judge nop
  //   judge sw
  //   calc MemtoReg
  //   calc SrcB
  //   calc ALUOp
  //   calcDMWr
  //   calc EXTOp
  //   calcRFWr
  //   calc RegDst
  //   calc NPCOp
endmodule

module no_need (
);

  wire ALUOp0, ALUOp1, ori, subu;

  buf or_1 (ALUOp0, subu);  // OR_Gate
  buf or_2 (ALUOp1, ori);  // OR_Gate

  // Notes on the sheet:
  //   ALUOp0
  //   ALUOp1
  //   ALUOp2
  //   temp ALUOp2 = 0 cause no need
endmodule
